// Logisim project ConWay16 (3).circ as structural Verilog: 2 circuits, main circuit main
module main (
  input  in_1,
  input  in_2,
  input  in_3,
  output out_4
);

  wire cdm_8_mark5_1_p2, cdm_8_mark5_1_p3, clock_1_out, clock_2_out, not_1_out;
  wire [7:0] cdm_8_mark5_1_p4, cdm_8_mark5_1_p5, cdm_8_mark5_1_p6, controlled_buffer_1_out;

  Clock clock_1 (.out(clock_1_out));
  D_Flip_Flop d_ff_1 (.clk(clock_1_out), .D(in_1), .Q(out_4), .preset(in_2), .reset(in_3));  // open: Qn, en
  Clock clock_2 (.out(clock_2_out));
  // CdM_8_mark5 cdm_8_mark5_1: pin names not known; wires that end beside it: clock_2_out, cdm_8_mark5_1_p2, cdm_8_mark5_1_p3, cdm_8_mark5_1_p4, cdm_8_mark5_1_p5, cdm_8_mark5_1_p6, cdm_8_mark5_1_p3
  assign controlled_buffer_1_out = not_1_out ? cdm_8_mark5_1_p5 : 8'bz;  // Controlled_Buffer controlled_buffer_1
  not not_1 (not_1_out, cdm_8_mark5_1_p3);
  assign cdm_8_mark5_1_p6 = cdm_8_mark5_1_p3 ? controlled_buffer_1_out : 8'bz;  // Controlled_Buffer controlled_buffer_2
  RAM ram_1 (
    .addr(cdm_8_mark5_1_p4), .data(controlled_buffer_1_out), .sel(cdm_8_mark5_1_p2), .clk(clock_2_out),
    .ld(cdm_8_mark5_1_p3));  // open: clr
endmodule

module \Матрица  (
);

  wire button_1_out, button_2_out, button_3_out, button_4_out, cl, ClR, not_1_out, or_1_out, or_2_out, y1,
       y2, y3, y4, y5, y6, y7, y8, y9, y10, y11, y12, y13, y14, y15, y16;
  wire [3:0] counter_1_q, counter_2_q;
  wire [15:0] _1, _2, _3, _4, _5, _6, _7, _8, _9, _10, _11, _12, _13, _14, _15, _16, demultiplexer_1_out0,
       demultiplexer_1_out1, demultiplexer_1_out2, demultiplexer_1_out3, demultiplexer_1_out4,
       demultiplexer_1_out5, demultiplexer_1_out6, demultiplexer_1_out7, demultiplexer_1_out8,
       demultiplexer_1_out9, demultiplexer_1_out10, demultiplexer_1_out11, demultiplexer_1_out12,
       demultiplexer_1_out13, demultiplexer_1_out14, demultiplexer_1_out15, demultiplexer_3_out0,
       demultiplexer_4_out0, demultiplexer_4_out1, demultiplexer_4_out2, demultiplexer_4_out3,
       demultiplexer_4_out4, demultiplexer_4_out5, demultiplexer_4_out6, demultiplexer_4_out7,
       demultiplexer_4_out8, demultiplexer_4_out9, demultiplexer_4_out10, demultiplexer_4_out11,
       demultiplexer_4_out12, demultiplexer_4_out13, demultiplexer_4_out14, demultiplexer_4_out15, or_3_out,
       or_4_out, or_5_out, or_6_out, or_7_out, or_8_out, or_9_out, or_10_out, or_11_out, or_12_out,
       or_13_out, or_14_out, or_15_out, or_16_out, or_17_out, or_18_out, Pixel, ram_1_data, shifter_1_out;

  Demultiplexer #(.select(4), .width(16), .enable("false")) demultiplexer_1 (
    .out0(demultiplexer_1_out0), .out1(demultiplexer_1_out1), .out2(demultiplexer_1_out2),
    .out3(demultiplexer_1_out3), .out4(demultiplexer_1_out4), .out5(demultiplexer_1_out5),
    .out6(demultiplexer_1_out6), .out7(demultiplexer_1_out7), .out8(demultiplexer_1_out8),
    .out9(demultiplexer_1_out9), .out10(demultiplexer_1_out10), .out11(demultiplexer_1_out11),
    .out12(demultiplexer_1_out12), .out13(demultiplexer_1_out13), .out14(demultiplexer_1_out14),
    .out15(demultiplexer_1_out15), .in(Pixel), .sel(counter_1_q));
  Demultiplexer #(.select(4), .enable("false")) demultiplexer_2 (
    .out0(y1), .out1(y2), .out2(y3), .out3(y4), .out4(y5), .out5(y6), .out6(y7), .out7(y8), .out8(y9),
    .out9(y10), .out10(y11), .out11(y12), .out12(y13), .out13(y14), .out14(y15), .out15(y16), .in(1'b1),
    .sel(counter_1_q));
  Register #(.width(16)) register_1 (.D(demultiplexer_1_out0), .en(y1), .Q(_1), .clk(cl), .clr(ClR));
  Register #(.width(16)) register_2 (.D(demultiplexer_1_out1), .en(y2), .Q(_2), .clk(cl), .clr(ClR));
  Register #(.width(16)) register_3 (.D(demultiplexer_1_out2), .en(y3), .Q(_3), .clk(cl), .clr(ClR));
  Register #(.width(16)) register_4 (.D(demultiplexer_1_out3), .en(y4), .Q(_4), .clk(cl), .clr(ClR));
  Register #(.width(16)) register_5 (.D(demultiplexer_1_out4), .en(y5), .Q(_5), .clk(cl), .clr(ClR));
  Register #(.width(16)) register_6 (.D(demultiplexer_1_out5), .en(y6), .Q(_6), .clk(cl), .clr(ClR));
  Register #(.width(16)) register_7 (.D(demultiplexer_1_out6), .en(y7), .Q(_7), .clk(cl), .clr(ClR));
  Register #(.width(16)) register_8 (.D(demultiplexer_1_out7), .en(y8), .Q(_8), .clk(cl), .clr(ClR));
  Register #(.width(16)) register_9 (.D(demultiplexer_1_out8), .en(y9), .Q(_9), .clk(cl), .clr(ClR));
  Register #(.width(16)) register_10 (.D(demultiplexer_1_out9), .en(y10), .Q(_10), .clk(cl), .clr(ClR));
  Register #(.width(16)) register_11 (.D(demultiplexer_1_out10), .en(y11), .Q(_11), .clk(cl), .clr(ClR));
  Register #(.width(16)) register_12 (.D(demultiplexer_1_out11), .en(y12), .Q(_12), .clk(cl), .clr(ClR));
  Register #(.width(16)) register_13 (.D(demultiplexer_1_out12), .en(y13), .Q(_13), .clk(cl), .clr(ClR));
  Register #(.width(16)) register_14 (.D(demultiplexer_1_out13), .en(y14), .Q(_14), .clk(cl), .clr(ClR));
  Register #(.width(16)) register_15 (.D(demultiplexer_1_out14), .en(y15), .Q(_15), .clk(cl), .clr(ClR));
  Register #(.width(16)) register_16 (.D(demultiplexer_1_out15), .en(y16), .Q(_16), .clk(cl), .clr(ClR));
  Button button_1 (.out(button_1_out));
  Button button_2 (.out(button_2_out));
  Button button_3 (.out(button_3_out));
  Button button_4 (.out(button_4_out));
  Clock clock_1 (.out(cl));
  Counter #(.width(4), .max('hf)) counter_1 (
    .load(button_1_out), .count(or_1_out), .Q(counter_1_q), .clk(or_1_out), .clr(ClR));  // open: D, carry
  or or_1 (or_1_out, button_1_out, button_3_out);
  Button \u_Очистка  (.out(ClR));
  or or_2 (or_2_out, button_2_out, button_4_out);
  Counter #(.width(4), .max('hf)) counter_2 (
    .load(button_4_out), .count(or_2_out), .Q(counter_2_q), .clk(or_2_out), .clr(ClR));  // open: D, carry
  assign or_3_out = demultiplexer_4_out0 | _1;  // OR_Gate or_3, 16 bits wide
  Demultiplexer #(.select(4), .enable("false")) demultiplexer_3 (
    .out0(demultiplexer_3_out0[0]), .out1(demultiplexer_3_out0[1]), .out2(demultiplexer_3_out0[2]),
    .out3(demultiplexer_3_out0[3]), .out4(demultiplexer_3_out0[4]), .out5(demultiplexer_3_out0[5]),
    .out6(demultiplexer_3_out0[6]), .out7(demultiplexer_3_out0[7]), .out8(demultiplexer_3_out0[8]),
    .out9(demultiplexer_3_out0[9]), .out10(demultiplexer_3_out0[10]), .out11(demultiplexer_3_out0[11]),
    .out12(demultiplexer_3_out0[12]), .out13(demultiplexer_3_out0[13]), .out14(demultiplexer_3_out0[14]),
    .out15(demultiplexer_3_out0[15]), .sel(counter_2_q));  // open: in
  assign or_4_out = demultiplexer_4_out3 | _4;  // OR_Gate or_4, 16 bits wide
  assign or_5_out = demultiplexer_4_out2 | _3;  // OR_Gate or_5, 16 bits wide
  assign or_6_out = demultiplexer_4_out1 | _2;  // OR_Gate or_6, 16 bits wide
  DotMatrix #(.matrixcols(16), .matrixrows(16)) dotmatrix_1 (
    .col0(or_3_out), .col1(or_6_out), .col2(or_5_out), .col3(or_4_out), .col4(or_8_out), .col5(or_7_out),
    .col6(or_11_out), .col7(or_9_out), .col8(or_10_out), .col9(or_12_out), .col10(or_14_out),
    .col11(or_13_out), .col12(or_16_out), .col13(or_15_out), .col14(or_18_out), .col15(or_17_out));
  assign or_7_out = demultiplexer_4_out5 | _6;  // OR_Gate or_7, 16 bits wide
  assign or_8_out = demultiplexer_4_out4 | _5;  // OR_Gate or_8, 16 bits wide
  assign or_9_out = _8 | demultiplexer_4_out7;  // OR_Gate or_9, 16 bits wide
  assign or_10_out = _9 | demultiplexer_4_out8;  // OR_Gate or_10, 16 bits wide
  assign or_11_out = demultiplexer_4_out6 | _7;  // OR_Gate or_11, 16 bits wide
  Demultiplexer #(.select(4), .width(16), .enable("false")) demultiplexer_4 (
    .out0(demultiplexer_4_out0), .out1(demultiplexer_4_out1), .out2(demultiplexer_4_out2),
    .out3(demultiplexer_4_out3), .out4(demultiplexer_4_out4), .out5(demultiplexer_4_out5),
    .out6(demultiplexer_4_out6), .out7(demultiplexer_4_out7), .out8(demultiplexer_4_out8),
    .out9(demultiplexer_4_out9), .out10(demultiplexer_4_out10), .out11(demultiplexer_4_out11),
    .out12(demultiplexer_4_out12), .out13(demultiplexer_4_out13), .out14(demultiplexer_4_out14),
    .out15(demultiplexer_4_out15), .in(demultiplexer_3_out0), .sel(counter_1_q));
  assign or_12_out = _10 | demultiplexer_4_out9;  // OR_Gate or_12, 16 bits wide
  assign or_13_out = _12 | demultiplexer_4_out11;  // OR_Gate or_13, 16 bits wide
  assign or_14_out = _11 | demultiplexer_4_out10;  // OR_Gate or_14, 16 bits wide
  assign or_15_out = _14 | demultiplexer_4_out13;  // OR_Gate or_15, 16 bits wide
  assign or_16_out = _13 | demultiplexer_4_out12;  // OR_Gate or_16, 16 bits wide
  assign or_17_out = _16 | demultiplexer_4_out15;  // OR_Gate or_17, 16 bits wide
  assign or_18_out = _15 | demultiplexer_4_out14;  // OR_Gate or_18, 16 bits wide
  assign Pixel = shifter_1_out | ram_1_data;  // OR_Gate or_19, 16 bits wide
  Button Enter ();  // open: out
  RAM #(.addrWidth(4), .dataWidth(16), .bus("separate")) ram_1 (
    .addr(counter_1_q), .din(Pixel), .data(ram_1_data), .str(1'b1), .clk(cl), .ld(1'b1));  // open: sel, clr
  not not_1 (not_1_out, cl);
  Shifter #(.width(16)) shifter_1 (.in(16'h1), .\dist (counter_2_q), .out(shifter_1_out));
endmodule
