// Logisim project GameOfLife.circ as structural Verilog: 1 circuit, main circuit main
module main (
);

  wire and_1_out, and_4_out, cdm_16_1_p4, cdm_16_1_p5, cdm_16_1_p7, cdm_16_1_p8, cdm_16_1_p9, Cl,
       comparator_1_eq, comparator_2_eq, comparator_3_gt, comparator_4_lt, comparator_5_eq, comparator_6_eq,
       COORD_sel, CURSOR_ON, data, decoder_1_out0, decoder_1_out1, decoder_1_out2, decoder_1_out3,
       decoder_1_out4, decoder_1_out5, decoder_1_out6, decoder_1_out7, decoder_1_out8, decoder_1_out9,
       decoder_1_out10, decoder_1_out11, decoder_1_out12, decoder_1_out13, decoder_1_out14, decoder_1_out15,
       Display_sel, DOWN_button, ENTER_button, IAck, IRP, IRQ, IS_RUNNING, KB_sel, LEFT_button, mem,
       not_1_out, not_2_out, not_3_out, not_4_out, not_5_out, not_6_out, not_7_out, not_9_out, not_11_out,
       not_12_out, not_13_out, not_14_out, not_15_out, not_16_out, or_19_out, or_20_out, read, RIGHT_button,
       s_r_ff_1_qn, UP_button, word;
  wire [1:0] counter_1_q;
  wire [1:1] KB_data;
  wire [3:0] subtractor_1_out, X_coord, Y_coord;
  wire [3:3] not_8_out;
  wire [15:0] address_bus, c1, c2, c3, c4, c5, c6, c7, c8, c9, c10, c11, c12, c13, c14, c15, c16,
       cdm_16_1_p15, cdm_16_1_p16, controlled_buffer_2_out, COORD_value, data_bus, demultiplexer_1_out0,
       KB_value, or_1_out, or_2_out, or_3_out, or_4_out, or_5_out, or_6_out, or_7_out, or_8_out, or_9_out,
       or_10_out, or_11_out, or_12_out, or_13_out, or_14_out, or_15_out, or_16_out, PROGRESS, register_1_q,
       register_2_q, register_3_q, register_4_q, register_5_q, register_7_q, register_9_q, register_10_q,
       register_11_q, register_12_q, register_13_q, register_14_q, register_15_q, register_16_q,
       register_17_q, register_18_q, tunnel;
  wire [15:1] IS_RUNNING_q;

  // Debugger debugger_1: pin names not known
  assign or_1_out = c2 | register_2_q;  // OR_Gate or_1, 16 bits wide
  assign or_2_out = c1 | register_1_q;  // OR_Gate or_2, 16 bits wide
  Register #(.width(16)) register_1 (.D(data_bus), .Q(register_1_q), .clk(decoder_1_out0));  // open: en, clr
  Register #(.width(16)) register_2 (.D(data_bus), .Q(register_2_q), .clk(decoder_1_out1));  // open: en, clr
  assign or_3_out = c4 | register_5_q;  // OR_Gate or_3, 16 bits wide
  assign or_4_out = c3 | register_3_q;  // OR_Gate or_4, 16 bits wide
  Register #(.width(16)) register_3 (.D(data_bus), .Q(register_3_q), .clk(decoder_1_out2));  // open: en, clr
  not not_1 (not_1_out, read);
  Comparator #(.width(16)) comparator_1 (.a(address_bus), .b(16'hfff6), .eq(comparator_1_eq));  // open: gt, lt
  assign or_5_out = c5 | register_4_q;  // OR_Gate or_5, 16 bits wide
  Register #(.width(16)) register_4 (.D(data_bus), .Q(register_4_q), .clk(decoder_1_out4));  // open: en, clr
  Register #(.width(16)) register_5 (.D(data_bus), .Q(register_5_q), .clk(decoder_1_out3));  // open: en, clr
  not not_2 (not_2_out, not_2_out);
  Register #(.width(16)) register_6 (.D(data_bus), .Q(PROGRESS), .clk(and_1_out));  // open: en, clr
  and and_1 (and_1_out, mem, not_1_out, comparator_1_eq, data);
  not not_3 (not_3_out, not_3_out);
  Comparator #(.width(16)) comparator_2 (.a(address_bus), .b(16'hfff0), .eq(comparator_2_eq));  // open: gt, lt
  assign or_6_out = c7 | register_10_q;  // OR_Gate or_6, 16 bits wide
  assign or_7_out = c6 | register_7_q;  // OR_Gate or_7, 16 bits wide
  Register #(.width(16)) register_7 (.D(data_bus), .Q(register_7_q), .clk(decoder_1_out5));  // open: en, clr
  Register #(.width(16)) register_8 (
    .D({{14{1'b0}}, KB_data[1], ENTER_button}), .Q(KB_value), .clk(IRP));  // open: en, clr
  assign or_8_out = c8 | register_9_q;  // OR_Gate or_8, 16 bits wide
  Register #(.width(16)) register_9 (.D(data_bus), .Q(register_9_q), .clk(decoder_1_out7));  // open: en, clr
  Register #(.width(16)) register_10 (.D(data_bus), .Q(register_10_q), .clk(decoder_1_out6));  // open: en, clr
  and and_2 (KB_sel, mem, read, comparator_2_eq, data);
  not not_4 (not_4_out, not_4_out);
  assign or_9_out = c10 | register_12_q;  // OR_Gate or_9, 16 bits wide
  assign or_10_out = c9 | register_11_q;  // OR_Gate or_10, 16 bits wide
  Register #(.width(16)) register_11 (.D(data_bus), .Q(register_11_q), .clk(decoder_1_out8));  // open: en, clr
  Register #(.width(16)) register_12 (.D(data_bus), .Q(register_12_q), .clk(decoder_1_out9));  // open: en, clr
  assign or_11_out = c11 | register_13_q;  // OR_Gate or_11, 16 bits wide
  assign or_12_out = c12 | register_14_q;  // OR_Gate or_12, 16 bits wide
  Register #(.width(16)) register_13 (.D(data_bus), .Q(register_13_q), .clk(decoder_1_out10));  // open: en, clr
  Decoder #(.select(4), .disabled(0)) decoder_1 (
    .out0(decoder_1_out0), .out1(decoder_1_out1), .out2(decoder_1_out2), .out3(decoder_1_out3),
    .out4(decoder_1_out4), .out5(decoder_1_out5), .out6(decoder_1_out6), .out7(decoder_1_out7),
    .out8(decoder_1_out8), .out9(decoder_1_out9), .out10(decoder_1_out10), .out11(decoder_1_out11),
    .out12(decoder_1_out12), .out13(decoder_1_out13), .out14(decoder_1_out14), .out15(decoder_1_out15),
    .sel({not_8_out[3], address_bus[3:1]}), .en(Display_sel));
  not not_5 (not_5_out, not_5_out);
  not not_6 (not_6_out, read);
  Comparator #(.width(16), .mode("unsigned")) comparator_3 (
    .a(address_bus), .b(16'hffcf), .gt(comparator_3_gt));  // open: eq, lt
  Comparator #(.width(16), .mode("unsigned")) comparator_4 (
    .a(address_bus), .b(16'hfff0), .lt(comparator_4_lt));  // open: gt, eq
  DotMatrix #(.inputtype("row"), .matrixcols(16), .matrixrows(1)) dotmatrix_1 (.row0(PROGRESS));
  DotMatrix #(.inputtype("row"), .matrixcols(16), .matrixrows(16)) dotmatrix_2 (
    .row0(or_2_out), .row1(or_1_out), .row2(or_4_out), .row3(or_3_out), .row4(or_5_out), .row5(or_7_out),
    .row6(or_6_out), .row7(or_8_out), .row8(or_10_out), .row9(or_9_out), .row10(or_11_out),
    .row11(or_12_out), .row12(or_13_out), .row13(or_15_out), .row14(or_14_out), .row15(or_16_out));
  assign or_13_out = c13 | register_15_q;  // OR_Gate or_13, 16 bits wide
  Register #(.width(16)) register_14 (.D(data_bus), .Q(register_14_q), .clk(decoder_1_out11));  // open: en, clr
  Register #(.width(16)) register_15 (.D(data_bus), .Q(register_15_q), .clk(decoder_1_out12));  // open: en, clr
  and and_3 (Display_sel, not_6_out, mem, data, comparator_3_gt, comparator_4_lt);
  not not_7 (not_7_out, read);
  Comparator #(.width(16)) comparator_5 (.a(address_bus), .b(16'hfff2), .eq(comparator_5_eq));  // open: gt, lt
  assign or_14_out = c15 | register_17_q;  // OR_Gate or_14, 16 bits wide
  assign or_15_out = c14 | register_16_q;  // OR_Gate or_15, 16 bits wide
  Register #(.width(16)) register_16 (.D(data_bus), .Q(register_16_q), .clk(decoder_1_out13));  // open: en, clr
  not not_8 (not_8_out[3], address_bus[4]);
  not not_9 (not_9_out, not_9_out);
  Register #(.width(16)) u_IS_RUNNING (.D(data_bus), .Q({IS_RUNNING_q, IS_RUNNING}), .clk(and_4_out));  // open: en, clr
  and and_4 (and_4_out, not_7_out, mem, comparator_5_eq, data);
  assign or_16_out = c16 | register_18_q;  // OR_Gate or_16, 16 bits wide
  Register #(.width(16)) register_17 (.D(data_bus), .Q(register_17_q), .clk(decoder_1_out14));  // open: en, clr
  Register #(.width(16)) register_18 (.D(data_bus), .Q(register_18_q), .clk(decoder_1_out15));  // open: en, clr
  not not_10 (CURSOR_ON, IS_RUNNING);
  Button button (.out(LEFT_button));
  or or_17 (IRP, ENTER_button, KB_data[1], 1'b0, 1'b0, 1'b0, 1'b0, 1'b0, 1'b0, 1'b0, 1'b0, 1'b0, 1'b0, 1'b0, 1'b0, 1'b0, 1'b0);
  not not_11 (not_11_out, not_11_out);
  Button button_2 (.out(UP_button));
  Button button_3 (.out(RIGHT_button));
  Button button_4 (.out(DOWN_button));
  not not_12 (not_12_out, not_12_out);
  S_R_Flip_Flop s_r_ff_1 (.S(1'b1), .clk(IRP), .R(1'b0), .Qn(s_r_ff_1_qn), .reset(IAck), .en(1'b1));  // open: Q, preset
  Counter #(.width(2), .max('h3), .ongoal("stay")) counter_1 (
    .load(1'b1), .D(2'b11), .count(s_r_ff_1_qn), .Q(counter_1_q), .clk(Cl));  // open: carry, clr
  Button button_5 (.out(KB_data[1]));
  Button button_6 (.out(ENTER_button));
  LED led_1 (.in(IS_RUNNING));
  or or_18 (IRQ, counter_1_q[0], counter_1_q[1]);
  // Probe on cdm_16_1_p4
  // CdM_16 cdm_16_1: pin names not known; wires that end beside it: IRQ, 6'b000101, IAck, cdm_16_1_p4, cdm_16_1_p5, Cl, cdm_16_1_p7, cdm_16_1_p8, cdm_16_1_p9, data, mem, read, word, address_bus, cdm_16_1_p15, cdm_16_1_p16
  // Probe on cdm_16_1_p5
  // Probe on cdm_16_1_p8
  // Probe on cdm_16_1_p7
  Clock clock_1 (.out(Cl));
  or or_19 (or_19_out, DOWN_button, UP_button);
  or or_20 (or_20_out, LEFT_button, RIGHT_button);
  not not_13 (not_13_out, not_13_out);
  Demultiplexer #(.select(4), .disabled(0)) demultiplexer_1 (
    .out0(demultiplexer_1_out0[0]), .out1(demultiplexer_1_out0[1]), .out2(demultiplexer_1_out0[2]),
    .out3(demultiplexer_1_out0[3]), .out4(demultiplexer_1_out0[4]), .out5(demultiplexer_1_out0[5]),
    .out6(demultiplexer_1_out0[6]), .out7(demultiplexer_1_out0[7]), .out8(demultiplexer_1_out0[8]),
    .out9(demultiplexer_1_out0[9]), .out10(demultiplexer_1_out0[10]), .out11(demultiplexer_1_out0[11]),
    .out12(demultiplexer_1_out0[12]), .out13(demultiplexer_1_out0[13]), .out14(demultiplexer_1_out0[14]),
    .out15(demultiplexer_1_out0[15]), .in(not_13_out), .sel(Y_coord), .en(CURSOR_ON));
  not not_14 (not_14_out, not_14_out);
  // Probe on cdm_16_1_p9
  Multiplexer #(.select(2), .width(16), .enable("false")) multiplexer_1 (
    .in0(controlled_buffer_2_out), .in1(KB_value), .in2(COORD_value), .in3(tunnel), .out(cdm_16_1_p16),
    .sel({COORD_sel, KB_sel}));
  Counter #(.width(4), .max('hf)) X (
    .load(UP_button), .count(or_19_out), .Q(X_coord), .clk(or_19_out));  // open: D, carry, clr
  Counter #(.width(4), .max('hf)) Y (
    .load(RIGHT_button), .count(or_20_out), .Q(Y_coord), .clk(or_20_out));  // open: D, carry, clr
  assign data_bus = not_15_out ? cdm_16_1_p15 : 16'bz;  // Controlled_Buffer controlled_buffer_1
  not not_15 (not_15_out, read);
  assign controlled_buffer_2_out = read ? data_bus : 16'bz;  // Controlled_Buffer controlled_buffer_2
  not not_16 (not_16_out, not_16_out);
  Subtractor #(.width(4)) subtractor_1 (.a(4'b1111), .b(Y_coord), .out(subtractor_1_out));  // open: bin, bout
  Demultiplexer #(.select(4), .width(16), .disabled(0)) demultiplexer_2 (
    .out0(c1), .out1(c2), .out2(c3), .out3(c4), .out4(c5), .out5(c6), .out6(c7), .out7(c8), .out8(c9),
    .out9(c10), .out10(c11), .out11(c12), .out12(c13), .out13(c14), .out14(c15), .out15(c16),
    .in(demultiplexer_1_out0), .sel(X_coord), .en(CURSOR_ON));
  // Probe on subtractor_1_out
  Comparator #(.width(16)) comparator_6 (.a(address_bus), .b(16'hfff4), .eq(comparator_6_eq));  // open: gt, lt
  Register #(.width(16)) register_19 (
    .D({subtractor_1_out, {8{1'b0}}, X_coord}), .Q(COORD_value), .clk(COORD_sel));  // open: en, clr
  // RAM ram_1: pin names not known; wires that end beside it: address_bus, word, mem, Cl, read, data_bus
  and and_5 (COORD_sel, mem, read, comparator_6_eq, data);

  // Other names for the same wires on the sheet: KB_data[0] = ENTER_button; PAUSE_button = KB_data[1]

  // Notes on the sheet:
  //   Playing Field
  //   Memory-mapped register selectors
  //   Game Button Controls
  //   Interrupt Conroller
  //   Cursor Controller
  //   CDM-16 with Von Neumann Architecture
endmodule
