// Logisim project proc_RAM.circ as structural Verilog: 1 circuit, main circuit main
module main (
  input  in_1,
  input  in_2,
  input  in_3,
  input  in_4,
  input  in_5,
  input  in_6
);

  wire and_3_out, and_4_out, and_5_out, and_6_out, and_7_out, and_8_out, and_9_out, and_10_out, and_11_out,
       and_12_out, and_13_out, and_14_out, and_15_out, and_16_out, and_17_out, and_18_out, and_19_out,
       and_20_out, and_21_out, and_22_out, and_23_out, and_24_out, and_25_out, and_26_out, and_27_out,
       and_28_out, and_29_out, and_30_out, and_31_out, and_32_out, and_33_out, and_34_out, cdm_8_mark5_1_p1,
       cdm_8_mark5_1_p2, cdm_8_mark5_1_p4, cdm_8_mark5_1_p5, cdm_8_mark5_1_p6, cdm_8_mark5_1_p7,
       cdm_8_mark5_1_p8, Cl, code, comparator_1_eq, comparator_2_eq, comparator_3_eq, comparator_4_eq,
       comparator_5_eq, comparator_6_eq, comparator_7_eq, comparator_8_eq, comparator_9_eq, comparator_10_eq,
       comparator_11_eq, comparator_12_eq, comparator_13_eq, comparator_14_eq, comparator_15_eq,
       comparator_16_eq, comparator_17_eq, comparator_18_eq, comparator_19_eq, comparator_20_eq,
       comparator_21_eq, comparator_22_eq, comparator_23_eq, comparator_24_eq, comparator_25_eq,
       comparator_26_eq, comparator_27_eq, comparator_28_eq, comparator_29_eq, comparator_30_eq,
       comparator_31_eq, comparator_32_eq, comparator_33_eq, comparator_34_eq, comparator_35_eq,
       comparator_36_eq, comparator_37_eq, comparator_38_eq, comparator_39_eq, comparator_40_eq,
       comparator_41_eq, comparator_42_eq, comparator_43_eq, comparator_44_eq, comparator_45_eq,
       comparator_46_eq, comparator_47_eq, comparator_48_eq, comparator_49_eq, comparator_50_eq,
       comparator_51_eq, comparator_52_eq, comparator_53_eq, comparator_54_eq, comparator_55_eq,
       comparator_56_eq, comparator_57_eq, comparator_58_eq, comparator_59_eq, comparator_60_eq,
       comparator_61_eq, comparator_62_eq, comparator_63_eq, comparator_64_eq, comparator_65_eq,
       comparator_66_eq, CORD_select, data, data_ins_prime, DOWN_button, IS_PAUSED, LEFT_button, memory,
       not_1_out, not_2_out, not_3_out, not_5_out, not_6_out, not_7_out, not_8_out, not_9_out, not_10_out,
       not_11_out, not_12_out, not_13_out, not_14_out, not_15_out, not_16_out, not_17_out, not_18_out,
       not_19_out, not_20_out, not_21_out, not_22_out, not_23_out, not_24_out, not_25_out, not_26_out,
       not_27_out, not_28_out, not_29_out, not_30_out, not_31_out, not_32_out, not_33_out, not_34_out,
       not_35_out, not_36_out, not_37_out, or_2_out, or_3_out, or_4_out, or_5_out, or_6_out, or_7_out,
       or_8_out, or_9_out, or_10_out, or_11_out, or_12_out, or_13_out, or_14_out, or_15_out, or_16_out,
       or_17_out, or_18_out, or_19_out, or_20_out, or_21_out, or_22_out, or_23_out, or_24_out, or_25_out,
       or_26_out, or_27_out, or_28_out, or_29_out, or_30_out, or_31_out, or_32_out, or_33_out, or_34_out,
       or_35_out, or_36_out, read_write_prime, RIGHT_button, STOP_out, STOP_select, UP_button;
  wire [0:0] register_1_q;
  wire [3:0] X_coord, Y_coord;
  wire [7:0] addr, cdm_8_mark5_1_p13, cdm_8_mark5_1_p14, D, multiplexer_1_out, or_1_out, ram_1_data,
       register_2_q, register_3_q, register_4_q, register_5_q, register_6_q, register_7_q, register_8_q,
       register_9_q, register_10_q, register_11_q, register_12_q, register_13_q, register_14_q,
       register_15_q, register_16_q, register_17_q, register_18_q, register_19_q, register_20_q,
       register_21_q, register_22_q, register_23_q, register_24_q, register_25_q, register_26_q,
       register_27_q, register_28_q, register_29_q, register_30_q, register_31_q, register_32_q,
       register_33_q;
  wire [15:0] column1, column2, column3, column4, column5, column6, column7, column8, column9, column10,
       column11, column12, column13, column14, column15, column16, cursor1, cursor2, cursor3, cursor4,
       cursor5, cursor6, cursor7, cursor8, cursor9, cursor10, cursor11, cursor12, cursor13, cursor14,
       cursor15, cursor16, decoder_2_out0, demultiplexer_1_out0;

  // Debugger debugger_1: pin names not known
  // Probe on cdm_8_mark5_1_p5
  // Probe on cdm_8_mark5_1_p2
  // Probe on cdm_8_mark5_1_p1
  // Probe on cdm_8_mark5_1_p4
  Clock clock_1 (.out(Cl));
  Comparator comparator_1 (.a(addr), .b(8'hf2), .eq(comparator_1_eq));  // open: gt, lt
  Button UP (.out(UP_button));
  Button LEFT (.out(LEFT_button));
  Button DOWN (.out(DOWN_button));
  // Probe on cdm_8_mark5_1_p7
  // Probe on cdm_8_mark5_1_p8
  // Probe on cdm_8_mark5_1_p6
  // CdM_8_mark5 cdm_8_mark5_1: pin names not known; wires that end beside it: cdm_8_mark5_1_p1, cdm_8_mark5_1_p2, Cl, cdm_8_mark5_1_p4, cdm_8_mark5_1_p5, cdm_8_mark5_1_p6, cdm_8_mark5_1_p7, cdm_8_mark5_1_p8, data_ins_prime, memory, read_write_prime, addr, cdm_8_mark5_1_p13, cdm_8_mark5_1_p14
  Button RIGHT (.out(RIGHT_button));
  Multiplexer #(.width(8)) multiplexer_1 (
    .in0({in_1, in_2, {6{in_1}}}), .in1({8{1'b0}}), .out(multiplexer_1_out), .sel(in_6));  // open: en
  assign or_1_out = {in_3, {2{in_5}}, in_3, {3{in_5}}, in_3} | multiplexer_1_out;  // OR_Gate or_1, 8 bits wide
  and and_1 (STOP_select, data_ins_prime, read_write_prime, comparator_1_eq);
  assign D = not_1_out ? cdm_8_mark5_1_p13 : 8'bz;  // Controlled_Buffer controlled_buffer_1
  not not_1 (not_1_out, read_write_prime);
  assign cdm_8_mark5_1_p14 = read_write_prime ? D : 8'bz;  // Controlled_Buffer controlled_buffer_2
  Button STOP (.out(STOP_out));
  not not_2 (not_2_out, not_2_out);
  Demultiplexer #(.select(4), .disabled(0)) demultiplexer_1 (
    .out0(demultiplexer_1_out0[0]), .out1(demultiplexer_1_out0[1]), .out2(demultiplexer_1_out0[2]),
    .out3(demultiplexer_1_out0[3]), .out4(demultiplexer_1_out0[4]), .out5(demultiplexer_1_out0[5]),
    .out6(demultiplexer_1_out0[6]), .out7(demultiplexer_1_out0[7]), .out8(demultiplexer_1_out0[8]),
    .out9(demultiplexer_1_out0[9]), .out10(demultiplexer_1_out0[10]), .out11(demultiplexer_1_out0[11]),
    .out12(demultiplexer_1_out0[12]), .out13(demultiplexer_1_out0[13]), .out14(demultiplexer_1_out0[14]),
    .out15(demultiplexer_1_out0[15]), .in(not_2_out), .sel(Y_coord), .en(IS_PAUSED));
  Decoder decoder_1 (.out0(code), .out1(data), .sel(data_ins_prime), .en(memory));
  not not_3 (not_3_out, register_1_q[0]);
  Register #(.width(1)) register_1 (.D(not_3_out), .Q(register_1_q[0]), .clk(STOP_out));  // open: en, clr
  not not_4 (IS_PAUSED, register_1_q[0]);
  Decoder #(.select(4), .enable("false")) decoder_2 (
    .out0(decoder_2_out0[0]), .out1(decoder_2_out0[1]), .out2(decoder_2_out0[2]), .out3(decoder_2_out0[3]),
    .out4(decoder_2_out0[4]), .out5(decoder_2_out0[5]), .out6(decoder_2_out0[6]), .out7(decoder_2_out0[7]),
    .out8(decoder_2_out0[8]), .out9(decoder_2_out0[9]), .out10(decoder_2_out0[10]),
    .out11(decoder_2_out0[11]), .out12(decoder_2_out0[12]), .out13(decoder_2_out0[13]),
    .out14(decoder_2_out0[14]), .out15(decoder_2_out0[15]), .sel(X_coord));
  Demultiplexer #(.select(4), .width(16), .disabled(0)) demultiplexer_2 (
    .out0(cursor1), .out1(cursor2), .out2(cursor3), .out3(cursor4), .out4(cursor5), .out5(cursor6),
    .out6(cursor7), .out7(cursor8), .out8(cursor9), .out9(cursor10), .out10(cursor11), .out11(cursor12),
    .out12(cursor13), .out13(cursor14), .out14(cursor15), .out15(cursor16), .in(demultiplexer_1_out0),
    .sel(X_coord), .en(IS_PAUSED));
  Counter #(.width(4), .max('hf)) u_X_coord (
    .load(LEFT_button), .count(or_2_out), .Q(X_coord), .clk(or_2_out));  // open: D, carry, clr
  or or_2 (or_2_out, RIGHT_button, LEFT_button);
  Counter #(.width(4), .max('hf)) u_Y_coord (
    .load(DOWN_button), .count(or_3_out), .Q(Y_coord), .clk(or_3_out));  // open: D, carry, clr
  or or_3 (or_3_out, UP_button, DOWN_button);
  ROM rom_1 (.addr(addr), .data(D), .sel(code));
  RAM ram_1 (.addr(addr), .data(ram_1_data), .sel(data), .clk(Cl), .ld(read_write_prime));  // open: clr
  or or_4 (or_4_out, STOP_select, CORD_select);
  assign D = STOP_select ? {{7{1'b0}}, register_1_q[0]} : 8'bz;  // Controlled_Buffer controlled_buffer_3
  Comparator comparator_2 (.a(addr), .b(8'hf3), .eq(comparator_2_eq));  // open: gt, lt
  assign ram_1_data = not_5_out ? D : 8'bz;  // Controlled_Buffer controlled_buffer_4
  not not_5 (not_5_out, or_4_out);
  assign D = CORD_select ? {Y_coord, X_coord} : 8'bz;  // Controlled_Buffer controlled_buffer_5
  DotMatrix #(.matrixcols(16), .matrixrows(16)) dotmatrix_1 (
    .col0(column1), .col1(column2), .col2(column3), .col3(column4), .col4(column5), .col5(column6),
    .col6(column7), .col7(column8), .col8(column9), .col9(column10), .col10(column11), .col11(column12),
    .col12(column13), .col13(column14), .col14(column15), .col15(column16));
  and and_2 (CORD_select, data_ins_prime, read_write_prime, comparator_2_eq);
  Comparator comparator_3 (.a(addr), .b(8'hb0), .eq(comparator_3_eq));  // open: gt, lt
  Comparator comparator_4 (.a(addr), .b(8'hd0), .eq(comparator_4_eq));  // open: gt, lt
  Comparator comparator_5 (.a(addr), .b(8'hb1), .eq(comparator_5_eq));  // open: gt, lt
  Comparator comparator_6 (.a(addr), .b(8'hd1), .eq(comparator_6_eq));  // open: gt, lt
  Comparator comparator_7 (.a(addr), .b(8'hb2), .eq(comparator_7_eq));  // open: gt, lt
  Comparator comparator_8 (.a(addr), .b(8'hd2), .eq(comparator_8_eq));  // open: gt, lt
  Comparator comparator_9 (.a(addr), .b(8'hb3), .eq(comparator_9_eq));  // open: gt, lt
  Comparator comparator_10 (.a(addr), .b(8'hd3), .eq(comparator_10_eq));  // open: gt, lt
  Comparator comparator_11 (.a(addr), .b(8'hb4), .eq(comparator_11_eq));  // open: gt, lt
  Comparator comparator_12 (.a(addr), .b(8'hd4), .eq(comparator_12_eq));  // open: gt, lt
  Comparator comparator_13 (.a(addr), .b(8'hb5), .eq(comparator_13_eq));  // open: gt, lt
  Comparator comparator_14 (.a(addr), .b(8'hd5), .eq(comparator_14_eq));  // open: gt, lt
  Comparator comparator_15 (.a(addr), .b(8'hb6), .eq(comparator_15_eq));  // open: gt, lt
  Comparator comparator_16 (.a(addr), .b(8'hd6), .eq(comparator_16_eq));  // open: gt, lt
  Comparator comparator_17 (.a(addr), .b(8'hb7), .eq(comparator_17_eq));  // open: gt, lt
  Comparator comparator_18 (.a(addr), .b(8'hd7), .eq(comparator_18_eq));  // open: gt, lt
  Comparator comparator_19 (.a(addr), .b(8'hb8), .eq(comparator_19_eq));  // open: gt, lt
  Comparator comparator_20 (.a(addr), .b(8'hd8), .eq(comparator_20_eq));  // open: gt, lt
  Comparator comparator_21 (.a(addr), .b(8'hb9), .eq(comparator_21_eq));  // open: gt, lt
  Comparator comparator_22 (.a(addr), .b(8'hd9), .eq(comparator_22_eq));  // open: gt, lt
  Comparator comparator_23 (.a(addr), .b(8'hba), .eq(comparator_23_eq));  // open: gt, lt
  Comparator comparator_24 (.a(addr), .b(8'hda), .eq(comparator_24_eq));  // open: gt, lt
  Comparator comparator_25 (.a(addr), .b(8'hbb), .eq(comparator_25_eq));  // open: gt, lt
  Comparator comparator_26 (.a(addr), .b(8'hdb), .eq(comparator_26_eq));  // open: gt, lt
  Comparator comparator_27 (.a(addr), .b(8'hbc), .eq(comparator_27_eq));  // open: gt, lt
  Comparator comparator_28 (.a(addr), .b(8'hdc), .eq(comparator_28_eq));  // open: gt, lt
  Comparator comparator_29 (.a(addr), .b(8'hbd), .eq(comparator_29_eq));  // open: gt, lt
  Comparator comparator_30 (.a(addr), .b(8'hdd), .eq(comparator_30_eq));  // open: gt, lt
  Comparator comparator_31 (.a(addr), .b(8'hbe), .eq(comparator_31_eq));  // open: gt, lt
  Comparator comparator_32 (.a(addr), .b(8'hde), .eq(comparator_32_eq));  // open: gt, lt
  Comparator comparator_33 (.a(addr), .b(8'hbf), .eq(comparator_33_eq));  // open: gt, lt
  Comparator comparator_34 (.a(addr), .b(8'hdf), .eq(comparator_34_eq));  // open: gt, lt
  Comparator comparator_35 (.a(addr), .b(8'hc0), .eq(comparator_35_eq));  // open: gt, lt
  Comparator comparator_36 (.a(addr), .b(8'he0), .eq(comparator_36_eq));  // open: gt, lt
  Comparator comparator_37 (.a(addr), .b(8'hc1), .eq(comparator_37_eq));  // open: gt, lt
  Comparator comparator_38 (.a(addr), .b(8'he1), .eq(comparator_38_eq));  // open: gt, lt
  Comparator comparator_39 (.a(addr), .b(8'hc2), .eq(comparator_39_eq));  // open: gt, lt
  Comparator comparator_40 (.a(addr), .b(8'he2), .eq(comparator_40_eq));  // open: gt, lt
  Comparator comparator_41 (.a(addr), .b(8'hc3), .eq(comparator_41_eq));  // open: gt, lt
  Comparator comparator_42 (.a(addr), .b(8'he3), .eq(comparator_42_eq));  // open: gt, lt
  Comparator comparator_43 (.a(addr), .b(8'hc4), .eq(comparator_43_eq));  // open: gt, lt
  Comparator comparator_44 (.a(addr), .b(8'he4), .eq(comparator_44_eq));  // open: gt, lt
  Comparator comparator_45 (.a(addr), .b(8'hc5), .eq(comparator_45_eq));  // open: gt, lt
  Comparator comparator_46 (.a(addr), .b(8'he5), .eq(comparator_46_eq));  // open: gt, lt
  Comparator comparator_47 (.a(addr), .b(8'hc6), .eq(comparator_47_eq));  // open: gt, lt
  Comparator comparator_48 (.a(addr), .b(8'he6), .eq(comparator_48_eq));  // open: gt, lt
  Comparator comparator_49 (.a(addr), .b(8'hc7), .eq(comparator_49_eq));  // open: gt, lt
  Comparator comparator_50 (.a(addr), .b(8'he7), .eq(comparator_50_eq));  // open: gt, lt
  Comparator comparator_51 (.a(addr), .b(8'hc8), .eq(comparator_51_eq));  // open: gt, lt
  Comparator comparator_52 (.a(addr), .b(8'he8), .eq(comparator_52_eq));  // open: gt, lt
  Comparator comparator_53 (.a(addr), .b(8'hc9), .eq(comparator_53_eq));  // open: gt, lt
  Comparator comparator_54 (.a(addr), .b(8'he9), .eq(comparator_54_eq));  // open: gt, lt
  Comparator comparator_55 (.a(addr), .b(8'hca), .eq(comparator_55_eq));  // open: gt, lt
  Comparator comparator_56 (.a(addr), .b(8'hea), .eq(comparator_56_eq));  // open: gt, lt
  Comparator comparator_57 (.a(addr), .b(8'hcb), .eq(comparator_57_eq));  // open: gt, lt
  Comparator comparator_58 (.a(addr), .b(8'heb), .eq(comparator_58_eq));  // open: gt, lt
  Comparator comparator_59 (.a(addr), .b(8'hcc), .eq(comparator_59_eq));  // open: gt, lt
  Comparator comparator_60 (.a(addr), .b(8'hec), .eq(comparator_60_eq));  // open: gt, lt
  Comparator comparator_61 (.a(addr), .b(8'hcd), .eq(comparator_61_eq));  // open: gt, lt
  Comparator comparator_62 (.a(addr), .b(8'hed), .eq(comparator_62_eq));  // open: gt, lt
  Comparator comparator_63 (.a(addr), .b(8'hce), .eq(comparator_63_eq));  // open: gt, lt
  Comparator comparator_64 (.a(addr), .b(8'hee), .eq(comparator_64_eq));  // open: gt, lt
  Comparator comparator_65 (.a(addr), .b(8'hcf), .eq(comparator_65_eq));  // open: gt, lt
  Comparator comparator_66 (.a(addr), .b(8'hef), .eq(comparator_66_eq));  // open: gt, lt
  or or_5 (or_5_out, comparator_3_eq, comparator_4_eq);
  or or_6 (or_6_out, comparator_5_eq, comparator_6_eq);
  or or_7 (or_7_out, comparator_7_eq, comparator_8_eq);
  or or_8 (or_8_out, comparator_9_eq, comparator_10_eq);
  or or_9 (or_9_out, comparator_11_eq, comparator_12_eq);
  or or_10 (or_10_out, comparator_13_eq, comparator_14_eq);
  or or_11 (or_11_out, comparator_15_eq, comparator_16_eq);
  or or_12 (or_12_out, comparator_17_eq, comparator_18_eq);
  or or_13 (or_13_out, comparator_19_eq, comparator_20_eq);
  or or_14 (or_14_out, comparator_21_eq, comparator_22_eq);
  or or_15 (or_15_out, comparator_23_eq, comparator_24_eq);
  or or_16 (or_16_out, comparator_25_eq, comparator_26_eq);
  or or_17 (or_17_out, comparator_27_eq, comparator_28_eq);
  or or_18 (or_18_out, comparator_29_eq, comparator_30_eq);
  or or_19 (or_19_out, comparator_31_eq, comparator_32_eq);
  or or_20 (or_20_out, comparator_33_eq, comparator_34_eq);
  or or_21 (or_21_out, comparator_35_eq, comparator_36_eq);
  or or_22 (or_22_out, comparator_37_eq, comparator_38_eq);
  or or_23 (or_23_out, comparator_39_eq, comparator_40_eq);
  or or_24 (or_24_out, comparator_41_eq, comparator_42_eq);
  or or_25 (or_25_out, comparator_43_eq, comparator_44_eq);
  or or_26 (or_26_out, comparator_45_eq, comparator_46_eq);
  or or_27 (or_27_out, comparator_47_eq, comparator_48_eq);
  or or_28 (or_28_out, comparator_49_eq, comparator_50_eq);
  or or_29 (or_29_out, comparator_51_eq, comparator_52_eq);
  or or_30 (or_30_out, comparator_53_eq, comparator_54_eq);
  or or_31 (or_31_out, comparator_55_eq, comparator_56_eq);
  or or_32 (or_32_out, comparator_57_eq, comparator_58_eq);
  or or_33 (or_33_out, comparator_59_eq, comparator_60_eq);
  or or_34 (or_34_out, comparator_61_eq, comparator_62_eq);
  or or_35 (or_35_out, comparator_63_eq, comparator_64_eq);
  or or_36 (or_36_out, comparator_65_eq, comparator_66_eq);
  not not_6 (not_6_out, read_write_prime);
  not not_7 (not_7_out, read_write_prime);
  not not_8 (not_8_out, read_write_prime);
  not not_9 (not_9_out, read_write_prime);
  not not_10 (not_10_out, read_write_prime);
  not not_11 (not_11_out, read_write_prime);
  not not_12 (not_12_out, read_write_prime);
  not not_13 (not_13_out, read_write_prime);
  not not_14 (not_14_out, read_write_prime);
  not not_15 (not_15_out, read_write_prime);
  not not_16 (not_16_out, read_write_prime);
  not not_17 (not_17_out, read_write_prime);
  not not_18 (not_18_out, read_write_prime);
  not not_19 (not_19_out, read_write_prime);
  not not_20 (not_20_out, read_write_prime);
  not not_21 (not_21_out, read_write_prime);
  not not_22 (not_22_out, read_write_prime);
  not not_23 (not_23_out, read_write_prime);
  not not_24 (not_24_out, read_write_prime);
  not not_25 (not_25_out, read_write_prime);
  not not_26 (not_26_out, read_write_prime);
  not not_27 (not_27_out, read_write_prime);
  not not_28 (not_28_out, read_write_prime);
  not not_29 (not_29_out, read_write_prime);
  not not_30 (not_30_out, read_write_prime);
  not not_31 (not_31_out, read_write_prime);
  not not_32 (not_32_out, read_write_prime);
  not not_33 (not_33_out, read_write_prime);
  not not_34 (not_34_out, read_write_prime);
  not not_35 (not_35_out, read_write_prime);
  not not_36 (not_36_out, read_write_prime);
  not not_37 (not_37_out, read_write_prime);
  and and_3 (and_3_out, or_5_out, memory, not_6_out, data_ins_prime);
  and and_4 (and_4_out, or_6_out, memory, not_7_out, data_ins_prime);
  and and_5 (and_5_out, or_7_out, memory, not_8_out, data_ins_prime);
  and and_6 (and_6_out, or_8_out, memory, not_9_out, data_ins_prime);
  and and_7 (and_7_out, or_9_out, memory, not_10_out, data_ins_prime);
  and and_8 (and_8_out, or_10_out, memory, not_11_out, data_ins_prime);
  and and_9 (and_9_out, or_11_out, memory, not_12_out, data_ins_prime);
  and and_10 (and_10_out, or_12_out, memory, not_13_out, data_ins_prime);
  and and_11 (and_11_out, or_13_out, memory, not_14_out, data_ins_prime);
  and and_12 (and_12_out, or_14_out, memory, not_15_out, data_ins_prime);
  and and_13 (and_13_out, or_15_out, memory, not_16_out, data_ins_prime);
  and and_14 (and_14_out, or_16_out, memory, not_17_out, data_ins_prime);
  and and_15 (and_15_out, or_17_out, memory, not_18_out, data_ins_prime);
  and and_16 (and_16_out, or_18_out, memory, not_19_out, data_ins_prime);
  and and_17 (and_17_out, or_19_out, memory, not_20_out, data_ins_prime);
  and and_18 (and_18_out, or_20_out, memory, not_21_out, data_ins_prime);
  and and_19 (and_19_out, or_21_out, memory, not_22_out, data_ins_prime);
  and and_20 (and_20_out, or_22_out, memory, not_23_out, data_ins_prime);
  and and_21 (and_21_out, or_23_out, memory, not_24_out, data_ins_prime);
  and and_22 (and_22_out, or_24_out, memory, not_25_out, data_ins_prime);
  and and_23 (and_23_out, or_25_out, memory, not_26_out, data_ins_prime);
  and and_24 (and_24_out, or_26_out, memory, not_27_out, data_ins_prime);
  and and_25 (and_25_out, or_27_out, memory, not_28_out, data_ins_prime);
  and and_26 (and_26_out, or_28_out, memory, not_29_out, data_ins_prime);
  and and_27 (and_27_out, or_29_out, memory, not_30_out, data_ins_prime);
  and and_28 (and_28_out, or_30_out, memory, not_31_out, data_ins_prime);
  and and_29 (and_29_out, or_31_out, memory, not_32_out, data_ins_prime);
  and and_30 (and_30_out, or_32_out, memory, not_33_out, data_ins_prime);
  and and_31 (and_31_out, or_33_out, memory, not_34_out, data_ins_prime);
  and and_32 (and_32_out, or_34_out, memory, not_35_out, data_ins_prime);
  and and_33 (and_33_out, or_35_out, memory, not_36_out, data_ins_prime);
  and and_34 (and_34_out, or_36_out, memory, not_37_out, data_ins_prime);
  Register register_2 (.D(D), .en(and_3_out), .Q(register_2_q), .clk(Cl));  // open: clr
  Register register_3 (.D(D), .en(and_4_out), .Q(register_3_q), .clk(Cl));  // open: clr
  Register register_4 (.D(D), .en(and_5_out), .Q(register_4_q), .clk(Cl));  // open: clr
  Register register_5 (.D(D), .en(and_6_out), .Q(register_5_q), .clk(Cl));  // open: clr
  Register register_6 (.D(D), .en(and_7_out), .Q(register_6_q), .clk(Cl));  // open: clr
  Register register_7 (.D(D), .en(and_8_out), .Q(register_7_q), .clk(Cl));  // open: clr
  Register register_8 (.D(D), .en(and_9_out), .Q(register_8_q), .clk(Cl));  // open: clr
  Register register_9 (.D(D), .en(and_10_out), .Q(register_9_q), .clk(Cl));  // open: clr
  Register register_10 (.D(D), .en(and_11_out), .Q(register_10_q), .clk(Cl));  // open: clr
  Register register_11 (.D(D), .en(and_12_out), .Q(register_11_q), .clk(Cl));  // open: clr
  Register register_12 (.D(D), .en(and_13_out), .Q(register_12_q), .clk(Cl));  // open: clr
  Register register_13 (.D(D), .en(and_14_out), .Q(register_13_q), .clk(Cl));  // open: clr
  Register register_14 (.D(D), .en(and_15_out), .Q(register_14_q), .clk(Cl));  // open: clr
  Register register_15 (.D(D), .en(and_16_out), .Q(register_15_q), .clk(Cl));  // open: clr
  Register register_16 (.D(D), .en(and_17_out), .Q(register_16_q), .clk(Cl));  // open: clr
  Register register_17 (.D(D), .en(and_18_out), .Q(register_17_q), .clk(Cl));  // open: clr
  Register register_18 (.D(D), .en(and_19_out), .Q(register_18_q), .clk(Cl));  // open: clr
  Register register_19 (.D(D), .en(and_20_out), .Q(register_19_q), .clk(Cl));  // open: clr
  Register register_20 (.D(D), .en(and_21_out), .Q(register_20_q), .clk(Cl));  // open: clr
  Register register_21 (.D(D), .en(and_22_out), .Q(register_21_q), .clk(Cl));  // open: clr
  Register register_22 (.D(D), .en(and_23_out), .Q(register_22_q), .clk(Cl));  // open: clr
  Register register_23 (.D(D), .en(and_24_out), .Q(register_23_q), .clk(Cl));  // open: clr
  Register register_24 (.D(D), .en(and_25_out), .Q(register_24_q), .clk(Cl));  // open: clr
  Register register_25 (.D(D), .en(and_26_out), .Q(register_25_q), .clk(Cl));  // open: clr
  Register register_26 (.D(D), .en(and_27_out), .Q(register_26_q), .clk(Cl));  // open: clr
  Register register_27 (.D(D), .en(and_28_out), .Q(register_27_q), .clk(Cl));  // open: clr
  Register register_28 (.D(D), .en(and_29_out), .Q(register_28_q), .clk(Cl));  // open: clr
  Register register_29 (.D(D), .en(and_30_out), .Q(register_29_q), .clk(Cl));  // open: clr
  Register register_30 (.D(D), .en(and_31_out), .Q(register_30_q), .clk(Cl));  // open: clr
  Register register_31 (.D(D), .en(and_32_out), .Q(register_31_q), .clk(Cl));  // open: clr
  Register register_32 (.D(D), .en(and_33_out), .Q(register_32_q), .clk(Cl));  // open: clr
  Register register_33 (.D(D), .en(and_34_out), .Q(register_33_q), .clk(Cl));  // open: clr
  assign column1 = cursor1 | {register_3_q, register_2_q};  // OR_Gate or_37, 16 bits wide
  assign column2 = cursor2 | {register_5_q, register_4_q};  // OR_Gate or_38, 16 bits wide
  assign column3 = cursor3 | {register_7_q, register_6_q};  // OR_Gate or_39, 16 bits wide
  assign column4 = cursor4 | {register_9_q, register_8_q};  // OR_Gate or_40, 16 bits wide
  assign column5 = cursor5 | {register_11_q, register_10_q};  // OR_Gate or_41, 16 bits wide
  assign column6 = cursor6 | {register_13_q, register_12_q};  // OR_Gate or_42, 16 bits wide
  assign column7 = cursor7 | {register_15_q, register_14_q};  // OR_Gate or_43, 16 bits wide
  assign column8 = cursor8 | {register_17_q, register_16_q};  // OR_Gate or_44, 16 bits wide
  assign column9 = cursor9 | {register_19_q, register_18_q};  // OR_Gate or_45, 16 bits wide
  assign column10 = cursor10 | {register_21_q, register_20_q};  // OR_Gate or_46, 16 bits wide
  assign column11 = cursor11 | {register_23_q, register_22_q};  // OR_Gate or_47, 16 bits wide
  assign column12 = cursor12 | {register_25_q, register_24_q};  // OR_Gate or_48, 16 bits wide
  assign column13 = cursor13 | {register_27_q, register_26_q};  // OR_Gate or_49, 16 bits wide
  assign column14 = cursor14 | {register_29_q, register_28_q};  // OR_Gate or_50, 16 bits wide
  assign column15 = cursor15 | {register_31_q, register_30_q};  // OR_Gate or_51, 16 bits wide
  assign column16 = cursor16 | {register_33_q, register_32_q};  // OR_Gate or_52, 16 bits wide

  assign in_4 = in_2;
  // also tied to GND on the sheet: {decoder_2_out0[0], decoder_2_out0[1], decoder_2_out0[2], decoder_2_out0[3], decoder_2_out0[4], decoder_2_out0[5], decoder_2_out0[6], decoder_2_out0[7], decoder_2_out0[8], decoder_2_out0[9], decoder_2_out0[10], decoder_2_out0[11], decoder_2_out0[12], decoder_2_out0[13], decoder_2_out0[14], decoder_2_out0[15]}

  // Notes on the sheet:
  //   contents of rom_1 (hex, n*v repeats v):
  //   d0 b0 88 c1 d1 9 a4 c5 cd 0 d0 ab d1 b0 a4 d1 ef a4 d0 0 d1 cf a4 d4
endmodule
